// Logisim project TempToLevelChipLevel.circ as structural Verilog: 1 circuit, main circuit main
module main (
  input  [5:0] set_temp,
  input  [5:0] amb_temp,
  output [2:0] out_3
);

  wire a, C4, n7408_1_pin6, n7408_1_pin8, n7408_1_pin11, n7432_1_pin11, n7486_1_pin2, n7486_1_pin3,
       n7486_1_pin4, n7486_1_pin5, n7486_1_pin7, n7486_1_pin9, n7486_1_pin11, n7486_1_pin12, n7486_1_pin14,
       n7486_2_pin2, n7486_2_pin3, n7486_2_pin5, n7486_2_pin6, n7486_2_pin8, n7486_2_pin10, n7486_2_pin11,
       n7486_2_pin13, n7486_3_pin3, n7486_3_pin6, n7486_3_pin8, n7486_3_pin11, n7486_4_pin2, n7486_4_pin5,
       n7486_4_pin8, n7486_4_pin11, n74283_1_pin1, n74283_1_pin4, n74283_2_pin1, n74283_2_pin4,
       n74283_2_pin7, n74283_2_pin10, n74283_3_pin9, S;

  _7486 #(.VccGndPorts("true")) u_7486_1 (
    .pin1(amb_temp[5]), .pin2(n7486_1_pin2), .pin3(n7486_1_pin3), .pin4(n7486_1_pin4), .pin5(n7486_1_pin5),
    .pin6(out_3[2]), .pin7(n7486_1_pin7), .pin14(n7486_1_pin14), .pin13(amb_temp[4]), .pin12(n7486_1_pin12),
    .pin11(n7486_1_pin11), .pin10(a), .pin9(n7486_1_pin9), .pin8(n7486_1_pin5));
  _7486 #(.VccGndPorts("true")) u_7486_2 (
    .pin1(amb_temp[2]), .pin2(n7486_2_pin2), .pin3(n7486_2_pin3), .pin4(amb_temp[3]), .pin5(n7486_2_pin5),
    .pin6(n7486_2_pin6), .pin7(n7486_1_pin7), .pin14(n7486_1_pin14), .pin13(n7486_2_pin13),
    .pin12(amb_temp[1]), .pin11(n7486_2_pin11), .pin10(n7486_2_pin10), .pin9(amb_temp[0]), .pin8(n7486_2_pin8));
  _7408 #(.VccGndPorts("true")) u_7408_1 (
    .pin4(C4), .pin5(n7486_1_pin11), .pin6(n7408_1_pin6), .pin7(n7486_1_pin7), .pin14(n7486_1_pin14),
    .pin13(C4), .pin12(set_temp[4]), .pin11(n7408_1_pin11), .pin10(n7486_1_pin11), .pin9(set_temp[4]),
    .pin8(n7408_1_pin8));  // open: pin1, pin2, pin3
  _74283 #(.VccGndPorts("true")) u_74283_1 (
    .pin1(n74283_1_pin1), .pin2(n7486_1_pin3), .pin3(set_temp[5]), .pin4(n74283_1_pin4), .pin5(set_temp[4]),
    .pin6(n7486_1_pin11), .pin7(C4), .pin8(n7486_1_pin7), .pin16(n7486_1_pin14), .pin13(a));  // open: pin15, pin14, pin12, pin11, pin10, pin9
  _74283 #(.VccGndPorts("true")) u_74283_2 (
    .pin1(n74283_2_pin1), .pin2(n7486_2_pin11), .pin3(set_temp[1]), .pin4(n74283_2_pin4), .pin5(set_temp[0]),
    .pin6(n7486_2_pin8), .pin7(n74283_2_pin7), .pin8(n7486_1_pin7), .pin16(n7486_1_pin14),
    .pin15(n7486_2_pin3), .pin14(set_temp[2]), .pin13(S), .pin12(set_temp[3]), .pin11(n7486_2_pin6),
    .pin10(n74283_2_pin10), .pin9(C4));
  _7432 #(.VccGndPorts("true")) u_7432_1 (
    .pin7(n7486_1_pin7), .pin14(n7486_1_pin14), .pin13(n7408_1_pin11), .pin12(n7408_1_pin8),
    .pin11(n7432_1_pin11), .pin10(n7432_1_pin11), .pin9(n7408_1_pin6), .pin8(n7486_1_pin9));  // open: pin1, pin2, pin3, pin4, pin5, pin6
  _7486 #(.VccGndPorts("true")) u_7486_3 (
    .pin1(n74283_2_pin10), .pin2(n7486_1_pin5), .pin3(n7486_3_pin3), .pin4(S), .pin5(n7486_1_pin5),
    .pin6(n7486_3_pin6), .pin7(n7486_1_pin7), .pin14(n7486_1_pin14), .pin13(n74283_2_pin1),
    .pin12(n7486_1_pin5), .pin11(n7486_3_pin11), .pin10(n74283_2_pin4), .pin9(n7486_1_pin5),
    .pin8(n7486_3_pin8));
  _7486 #(.VccGndPorts("true")) u_7486_4 (
    .pin1(n7486_1_pin5), .pin2(n7486_4_pin2), .pin3(out_3[1]), .pin4(n7486_1_pin5), .pin5(n7486_4_pin5),
    .pin6(out_3[0]), .pin7(n7486_1_pin7), .pin14(n7486_1_pin14), .pin13(n74283_1_pin4), .pin12(n7486_1_pin5),
    .pin11(n7486_4_pin11), .pin10(n74283_1_pin1), .pin9(n7486_1_pin5), .pin8(n7486_4_pin8));
  _74283 #(.VccGndPorts("true")) u_74283_3 (
    .pin3(n7486_3_pin11), .pin5(n7486_3_pin8), .pin7(n7486_1_pin5), .pin8(n7486_1_pin7),
    .pin16(n7486_1_pin14), .pin14(n7486_3_pin6), .pin12(n7486_3_pin3), .pin9(n74283_3_pin9));  // open: pin1, pin2, pin4, pin6, pin15, pin13, pin11, pin10
  _74283 #(.VccGndPorts("true")) u_74283_4 (
    .pin1(n7486_4_pin2), .pin3(n7486_4_pin8), .pin4(n7486_4_pin5), .pin5(n7486_4_pin11),
    .pin7(n74283_3_pin9), .pin8(n7486_1_pin7), .pin16(n7486_1_pin14));  // open: pin2, pin6, pin15, pin14, pin13, pin12, pin11, pin10, pin9
  // also tied to GND on the sheet: n7486_1_pin7
  // also tied to VCC on the sheet: {n7486_1_pin2, n7486_2_pin13, n7486_2_pin2, n7486_1_pin12, n7486_1_pin4, n7486_2_pin10, n7486_2_pin5, n74283_2_pin7, n7486_1_pin14}
endmodule
