// Logisim project Final.circ as structural Verilog: 1 circuit, main circuit workordie
module workordie (
);

  wire clock_1_out, clock_2_out, digital_oscilloscope_1_p1, faultqueue_1_x, not_1_out, speedtopwm_1_pwmout;
  wire [2:0] leveltofanspeed_1_c, temptolevel_1_levelout;
  wire [5:0] slider_1_out, slider_2_out;

  Slider #(.value('h21), .width(6)) slider_1 (.out(slider_1_out));
  Slider #(.value('h2b), .width(6)) slider_2 (.out(slider_2_out));
  Clock #(.highDuration(32), .lowDuration(32)) clock_1 (.out(clock_1_out));
  Clock clock_2 (.out(clock_2_out));
  // Digital_Oscilloscope #(.showclock("false")) digital_oscilloscope_1: pin names not known; wires that end beside it: digital_oscilloscope_1_p1, clock_2_out
  tempToLevel temptolevel_1 (.sensed(slider_1_out), .desired(slider_2_out), .LevelOut(temptolevel_1_levelout));
  faultqueue faultqueue_1 (.Clk(clock_1_out), .Tin(slider_1_out), .X(faultqueue_1_x));
  levelToFanspeed leveltofanspeed_1 (
    .X(temptolevel_1_levelout[2]), .Y(temptolevel_1_levelout[1]), .Z(temptolevel_1_levelout[0]),
    .CLK(clock_1_out), .A(leveltofanspeed_1_c[2]), .B(leveltofanspeed_1_c[1]), .C(leveltofanspeed_1_c[0]));  // open: A_bar, B_bar, C_bar
  SpeedToPWM speedtopwm_1 (
    .S2(leveltofanspeed_1_c[2]), .S1(leveltofanspeed_1_c[1]), .S0(leveltofanspeed_1_c[0]), .Clk(clock_2_out),
    .PWMOut(speedtopwm_1_pwmout));
  not not_1 (not_1_out, faultqueue_1_x);
  and and_1 (digital_oscilloscope_1_p1, speedtopwm_1_pwmout, not_1_out);
  // Probe on temptolevel_1_levelout
  // Probe on leveltofanspeed_1_c

  // Notes on the sheet:
  //   Sensor input temp.
  //   User input temp.
  //   tempDiffToLevel
endmodule
