// Logisim project LevelToFanSpeedChipLevel.circ as structural Verilog: 1 circuit, main circuit main
module main (
  input  [2:0] XYZ
);

  wire a, ABC_pin9, b, c, n7400_1_pin7, n7400_1_pin8, n7400_1_pin11, n7400_1_pin14, n7408_1_pin3,
       n7408_1_pin6, n7408_1_pin8, n7408_1_pin9, n7411_1_pin6, n7411_1_pin8, n7411_1_pin9, n7411_1_pin12,
       n7411_1_pin13, n7411_2_pin6, n7411_2_pin8, n7411_2_pin12, n7411_3_pin1, n7411_3_pin6, n7411_3_pin10,
       n7421_1_pin1, n7421_1_pin5, n7421_1_pin6, n7421_1_pin8, n7421_1_pin9, n7421_2_pin8, n7421_3_pin6,
       n7421_3_pin8, n7421_4_pin6, n7421_4_pin8, n7421_5_pin8, n7432_1_pin3, n7432_1_pin5, n7432_1_pin6,
       n7432_1_pin11, n7432_2_pin3, n7432_2_pin6, n7432_2_pin8, n7432_2_pin11, n7432_3_pin2, n7432_3_pin3,
       n7432_3_pin5, n7432_3_pin6, n7432_4_pin2, n7432_4_pin3, n7432_4_pin6;

  _7400 #(.VccGndPorts("true")) u_7400_1 (
    .pin1(XYZ[0]), .pin2(XYZ[0]), .pin3(a), .pin7(n7400_1_pin7), .pin14(n7400_1_pin14), .pin13(XYZ[2]),
    .pin12(XYZ[2]), .pin11(n7400_1_pin11), .pin10(XYZ[1]), .pin9(XYZ[1]), .pin8(n7400_1_pin8));  // open: pin4, pin5, pin6
  _7411 #(.VccGndPorts("true")) u_7411_1 (
    .pin1(XYZ[2]), .pin2(XYZ[2]), .pin3(XYZ[2]), .pin4(XYZ[1]), .pin5(XYZ[0]), .pin6(n7411_1_pin6),
    .pin7(n7400_1_pin7), .pin14(n7400_1_pin14), .pin13(n7411_1_pin13), .pin12(n7411_1_pin12), .pin11(XYZ[1]),
    .pin10(XYZ[2]), .pin9(n7411_1_pin9), .pin8(n7411_1_pin8));
  _7411 #(.VccGndPorts("true")) u_7411_2 (
    .pin1(XYZ[2]), .pin2(n7411_1_pin9), .pin3(XYZ[1]), .pin4(XYZ[2]), .pin5(b), .pin6(n7411_2_pin6),
    .pin7(n7400_1_pin7), .pin14(n7400_1_pin14), .pin13(b), .pin12(n7411_2_pin12), .pin11(XYZ[0]),
    .pin10(XYZ[2]), .pin9(b), .pin8(n7411_2_pin8));
  _7421 #(.VccGndPorts("true")) u_7421_1 (
    .pin1(n7421_1_pin1), .pin2(a), .pin4(b), .pin5(n7421_1_pin5), .pin6(n7421_1_pin6), .pin7(n7400_1_pin7),
    .pin14(n7400_1_pin14), .pin13(a), .pin12(XYZ[1]), .pin10(n7421_1_pin5), .pin9(n7421_1_pin9),
    .pin8(n7421_1_pin8));  // open: pin3, pin11
  _7411 #(.VccGndPorts("true")) u_7411_3 (
    .pin1(n7411_3_pin1), .pin2(n7421_1_pin1), .pin3(XYZ[0]), .pin4(n7400_1_pin8), .pin5(n7421_1_pin9),
    .pin6(n7411_3_pin6), .pin7(n7400_1_pin7), .pin14(n7400_1_pin14), .pin13(n7411_1_pin9), .pin12(c),
    .pin11(XYZ[2]), .pin10(n7411_3_pin10), .pin9(n7411_3_pin1), .pin8(n7421_1_pin9));
  _7408 #(.VccGndPorts("true")) u_7408_1 (
    .pin1(XYZ[1]), .pin2(n7400_1_pin11), .pin3(n7408_1_pin3), .pin4(n7408_1_pin3), .pin5(n7411_1_pin13),
    .pin6(n7408_1_pin6), .pin7(n7400_1_pin7), .pin14(n7400_1_pin14), .pin13(n7400_1_pin8), .pin12(XYZ[2]),
    .pin11(n7421_1_pin1), .pin10(a), .pin9(n7408_1_pin9), .pin8(n7408_1_pin8));
  _7421 #(.VccGndPorts("true")) u_7421_2 (
    .pin1(XYZ[2]), .pin2(n7411_3_pin10), .pin4(n7411_3_pin1), .pin5(n7421_1_pin5), .pin6(n7408_1_pin9),
    .pin7(n7400_1_pin7), .pin14(n7400_1_pin14), .pin13(XYZ[0]), .pin12(n7408_1_pin3), .pin10(b),
    .pin9(n7411_1_pin9), .pin8(n7421_2_pin8));  // open: pin3, pin11
  _7421 #(.VccGndPorts("true")) u_7421_3 (
    .pin1(n7408_1_pin3), .pin2(b), .pin4(n7421_1_pin5), .pin5(XYZ[0]), .pin6(n7421_3_pin6),
    .pin7(n7400_1_pin7), .pin14(n7400_1_pin14), .pin13(XYZ[0]), .pin12(n7411_3_pin1), .pin10(n7411_1_pin9),
    .pin9(n7421_1_pin1), .pin8(n7421_3_pin8));  // open: pin3, pin11
  _7421 #(.VccGndPorts("true")) u_7421_4 (
    .pin1(a), .pin2(n7411_3_pin10), .pin4(n7421_1_pin5), .pin5(n7421_1_pin1), .pin6(n7421_4_pin6),
    .pin7(n7400_1_pin7), .pin14(n7400_1_pin14), .pin13(n7408_1_pin3), .pin12(b), .pin10(a),
    .pin9(n7411_1_pin9), .pin8(n7421_4_pin8));  // open: pin3, pin11
  _7421 #(.VccGndPorts("true")) u_7421_5 (
    .pin7(n7400_1_pin7), .pin14(n7400_1_pin14), .pin13(XYZ[0]), .pin12(XYZ[0]), .pin10(n7400_1_pin11),
    .pin9(n7411_1_pin13), .pin8(n7421_5_pin8));  // open: pin1, pin2, pin3, pin4, pin5, pin6, pin11
  _7432 #(.VccGndPorts("true")) u_7432_1 (
    .pin1(n7411_2_pin6), .pin2(n7411_2_pin12), .pin3(n7432_1_pin3), .pin4(n7432_1_pin3), .pin5(n7432_1_pin5),
    .pin6(n7432_1_pin6), .pin7(n7400_1_pin7), .pin14(n7400_1_pin14), .pin13(n7411_1_pin6),
    .pin12(n7411_1_pin12), .pin11(n7432_1_pin11), .pin10(n7411_1_pin8), .pin9(n7411_2_pin8),
    .pin8(n7432_1_pin5));
  _7432 #(.VccGndPorts("true")) u_7432_2 (
    .pin1(n7421_1_pin8), .pin2(n7411_3_pin6), .pin3(n7432_2_pin3), .pin4(c), .pin5(n7432_2_pin3),
    .pin6(n7432_2_pin6), .pin7(n7400_1_pin7), .pin14(n7400_1_pin14), .pin13(n7421_1_pin6),
    .pin12(n7408_1_pin6), .pin11(n7432_2_pin11), .pin10(n7432_1_pin6), .pin9(n7432_1_pin11),
    .pin8(n7432_2_pin8));
  _7432 #(.VccGndPorts("true")) u_7432_3 (
    .pin1(n7421_3_pin6), .pin2(n7432_3_pin2), .pin3(n7432_3_pin3), .pin4(n7421_2_pin8), .pin5(n7432_3_pin5),
    .pin6(n7432_3_pin6), .pin7(n7400_1_pin7), .pin14(n7400_1_pin14), .pin13(n7421_3_pin8),
    .pin12(n7408_1_pin8), .pin11(n7432_3_pin2), .pin10(n7432_2_pin6), .pin9(n7432_2_pin11),
    .pin8(n7432_3_pin5));
  _7432 #(.VccGndPorts("true")) u_7432_4 (
    .pin1(n7421_4_pin6), .pin2(n7432_4_pin2), .pin3(n7432_4_pin3), .pin4(n7432_4_pin3), .pin5(n7421_5_pin8),
    .pin6(n7432_4_pin6), .pin7(n7400_1_pin7), .pin14(n7400_1_pin14), .pin13(n7432_3_pin3),
    .pin12(n7421_4_pin8), .pin11(n7432_4_pin2));  // open: pin10, pin9, pin8
  _74175 #(.VccGndPorts("true")) ABC (
    .pin2(n7411_1_pin13), .pin3(n7411_3_pin10), .pin4(n7432_2_pin8), .pin5(n7432_3_pin6),
    .pin6(n7411_3_pin1), .pin7(b), .pin8(n7400_1_pin7), .pin16(n7400_1_pin14), .pin12(n7432_4_pin6),
    .pin11(n7421_1_pin5), .pin10(n7411_1_pin9), .pin9(ABC_pin9));  // open: pin1, pin15, pin14, pin13
  Clock clock_1 (.out(ABC_pin9));
  // Probe on n7411_1_pin13
  // Probe on b
  // Probe on n7411_1_pin9
  // also tied to GND on the sheet: n7400_1_pin7
  // also tied to VCC on the sheet: n7400_1_pin14

  // Notes on the sheet:
  //   X'Y
  //   XY'
  //   XY'
endmodule
