// Logisim project lib_FaultQueue.circ as structural Verilog: 2 circuits, main circuit faultqueue
module faultqueue (
  input  Clk,
  input  [5:0] Tin,
  output X
);

  wire and_1_out, and_2_out, and_3_out, and_4_out, and_5_out, and_6_out, shift_register_1_p3,
       shift_register_1_p4, shift_register_1_p5;

  and and_1 (and_1_out, Tin[5], Tin[4]);
  and and_2 (and_2_out, Tin[3], Tin[2]);
  and and_3 (and_3_out, Tin[1], Tin[0]);
  and and_4 (and_4_out, and_1_out, and_2_out);
  and and_5 (and_5_out, and_4_out, and_3_out);
  // Shift_Register #(.length(3)) shift_register_1: pin names not known; wires that end beside it: Clk, and_5_out, shift_register_1_p3, shift_register_1_p4, shift_register_1_p5
  and and_6 (and_6_out, shift_register_1_p3, shift_register_1_p4);
  and and_7 (X, and_6_out, shift_register_1_p5);
endmodule

module testSandbox325235 (
);

  wire clock_1_out, faultqueue_1_p4;
  wire [5:0] slider_1_out;

  Slider #(.value('h3f), .width(6)) slider_1 (.out(slider_1_out));
  Clock clock_1 (.out(clock_1_out));
  // faultqueue faultqueue_1: pin names not known; wires that end beside it: slider_1_out[0], slider_1_out[1], slider_1_out[2], faultqueue_1_p4
endmodule
