// Logisim project lib_SpeedToPWM.circ as structural Verilog: 2 circuits, main circuit SpeedToPWM
module SpeedToPWM (
  input  S2,
  input  S1,
  input  S0,
  input  Clk,
  output PWMOut
);

  wire comparator_1_gt;
  wire [1:0] counter_1_q;

  Counter #(.max('h3), .width(2)) counter_1 (.Q(counter_1_q), .clk(Clk));  // open: load, D, count, carry, up, clr
  Comparator #(.mode("unsigned"), .width(2)) comparator_1 (
    .a({S1, S0}), .b(counter_1_q), .gt(comparator_1_gt));  // open: eq, lt
  or or_1 (PWMOut, S2, comparator_1_gt);
endmodule

module testSandbox2353525 (
);

  wire clock_1_out, digital_oscilloscope_1_p2;
  wire [2:0] slider_1_out;

  Slider #(.width(3)) slider_1 (.out(slider_1_out));
  Clock clock_1 (.out(clock_1_out));
  // Digital_Oscilloscope digital_oscilloscope_1: pin names not known; wires that end beside it: clock_1_out, digital_oscilloscope_1_p2
  SpeedToPWM speedtopwm_1 (
    .S2(slider_1_out[2]), .S1(slider_1_out[1]), .S0(slider_1_out[0]), .Clk(clock_1_out),
    .PWMOut(digital_oscilloscope_1_p2));
endmodule
