// Logisim project lib_TempToLevel.circ as structural Verilog: 2 circuits, main circuit tempToLevel
module tempToLevel (
  input  [5:0] sensed,
  input  [5:0] desired,
  output [2:0] LevelOut
);

  wire [5:0] adder_1_out, subtractor_1_out, xor_1_out;
  wire [5:5] subtractor_1_bout;

  // Probe on sensed
  // Probe on desired
  Subtractor #(.width(6)) subtractor_1 (
    .a(sensed), .b(desired), .out(subtractor_1_out), .bout(subtractor_1_bout[5]));  // open: bin
  assign xor_1_out = subtractor_1_out ^ {6{subtractor_1_bout[5]}};  // XOR_Gate xor_1, 6 bits wide
  Adder #(.width(6)) adder_1 (
    .a(xor_1_out), .b({6{1'b0}}), .out(adder_1_out), .cin(subtractor_1_bout[5]));  // open: cout
  // Probe on adder_1_out
  // Probe on {subtractor_1_bout[5], adder_1_out[5:4]}
  not not_1 (LevelOut[2], subtractor_1_bout[5]);
  xor xor_2 (LevelOut[1], subtractor_1_bout[5], adder_1_out[5]);
  xor xor_3 (LevelOut[0], subtractor_1_bout[5], adder_1_out[4]);

  // Notes on the sheet:
  //   Set Temperature
  //   Ambient Temperature
  //   A
endmodule

module testSandbox5532 (
);

  wire clock_1_out;
  wire [2:0] temptolevel_1_levelout;
  wire [5:0] slider_1_out, slider_2_out;

  Slider #(.value('h3b), .width(6)) slider_1 (.out(slider_1_out));
  Slider #(.value('h3e), .width(6)) slider_2 (.out(slider_2_out));
  Clock clock_1 (.out(clock_1_out));
  tempToLevel temptolevel_1 (.sensed(slider_1_out), .desired(slider_1_out), .LevelOut(temptolevel_1_levelout));
  // Probe on temptolevel_1_levelout
endmodule
