// Logisim project lib_userTempSet.circ as structural Verilog
module TTL_NORwithNANDquad (
  input  Gnd,
  input  In2,
  input  In1,
  input  Vcc,
  output Out1
);

  wire n7400_1_pin1, n7400_1_pin2, n7400_1_pin3;

  _7400 #(.VccGndPorts("true")) u_7400_1 (
    .pin1(n7400_1_pin1), .pin2(n7400_1_pin2), .pin3(n7400_1_pin3), .pin4(n7400_1_pin3), .pin5(n7400_1_pin3),
    .pin6(Out1), .pin7(Gnd), .pin14(Vcc), .pin13(In1), .pin12(In1), .pin11(n7400_1_pin1), .pin10(In2),
    .pin9(In2), .pin8(n7400_1_pin2));
endmodule

module diag_Tset (
  input  In0,
  input  in1,
  output [5:0] Output6b
);

  wire nor_1_out;
  wire [5:0] adder_1_out, multiplexer_1_out;

  Adder #(.width(6)) adder_1 (.a(Output6b), .b(multiplexer_1_out), .out(adder_1_out));  // open: cin, cout
  Multiplexer #(.enable("false"), .width(6)) multiplexer_1 (
    .in0(6'b000001), .in1({6{1'b1}}), .out(multiplexer_1_out), .sel(In0));
  Register #(.width(6)) register_1 (.D(adder_1_out), .Q(Output6b), .clk(nor_1_out));  // open: en, clr
  nor nor_1 (nor_1_out, In0, in1);

  // Notes on the sheet:
  //   decrement
  //   increment
endmodule

module TTL_6bRegister (
  input  [5:0] Input6bits,
  input  Reset,
  input  Vcc,
  input  Clk,
  input  Gnd,
  output [5:0] Out6bits
);

  _7474 #(.ShowInternalStructure("true"), .VccGndPorts("true")) u_7474_1 (
    .pin1(Reset), .pin2(Input6bits[4]), .pin3(Clk), .pin4(Vcc), .pin5(Out6bits[4]), .pin7(Gnd), .pin14(Vcc),
    .pin13(Reset), .pin12(Input6bits[5]), .pin11(Clk), .pin10(Vcc), .pin9(Out6bits[5]));  // open: pin6, pin8
  _7474 #(.ShowInternalStructure("true"), .VccGndPorts("true")) u_7474_2 (
    .pin1(Reset), .pin2(Input6bits[2]), .pin3(Clk), .pin4(Vcc), .pin5(Out6bits[2]), .pin7(Gnd), .pin14(Vcc),
    .pin13(Reset), .pin12(Input6bits[3]), .pin11(Clk), .pin10(Vcc), .pin9(Out6bits[3]));  // open: pin6, pin8
  _7474 #(.ShowInternalStructure("true"), .VccGndPorts("true")) u_7474_3 (
    .pin1(Reset), .pin2(Input6bits[0]), .pin3(Clk), .pin4(Vcc), .pin5(Out6bits[0]), .pin7(Gnd), .pin14(Vcc),
    .pin13(Reset), .pin12(Input6bits[1]), .pin11(Clk), .pin10(Vcc), .pin9(Out6bits[1]));  // open: pin6, pin8
endmodule

module TTL_2x1MUXwithNANDquad (
  input  Gnd,
  input  S,
  input  In0,
  input  Vcc,
  input  In1,
  output Out1
);

  wire n7400_1_pin3, n7400_1_pin4, n7400_1_pin12;

  _7400 #(.VccGndPorts("true")) u_7400_1 (
    .pin1(In1), .pin2(S), .pin3(n7400_1_pin3), .pin4(n7400_1_pin4), .pin5(n7400_1_pin3), .pin6(Out1),
    .pin7(Gnd), .pin14(Vcc), .pin13(In0), .pin12(n7400_1_pin12), .pin11(n7400_1_pin4), .pin10(S), .pin9(S),
    .pin8(n7400_1_pin12));
endmodule

module TTL_8bitadder_stupid (
  input  Gnd,
  input  [7:0] B8bits,
  input  Vcc,
  input  [7:0] in_4,
  input  [7:0] A8bits
);

  wire n74283_1_pin7;

  _74283 #(.ShowInternalStructure("true"), .VccGndPorts("true")) u_74283_1 (
    .pin2(B8bits[5]), .pin3(A8bits[5]), .pin5(A8bits[4]), .pin6(B8bits[4]), .pin7(n74283_1_pin7), .pin8(Gnd),
    .pin16(Vcc), .pin15(B8bits[6]), .pin14(A8bits[6]), .pin12(A8bits[7]), .pin11(B8bits[7]));  // open: pin1, pin4, pin13, pin10, pin9
  _74283 #(.ShowInternalStructure("true"), .VccGndPorts("true")) u_74283_2 (
    .pin2(B8bits[1]), .pin3(A8bits[1]), .pin5(A8bits[0]), .pin6(B8bits[0]), .pin8(Gnd), .pin16(Vcc),
    .pin15(B8bits[2]), .pin14(A8bits[2]), .pin12(A8bits[3]), .pin11(B8bits[3]), .pin9(n74283_1_pin7));  // open: pin1, pin4, pin7, pin13, pin10

  // Notes on the sheet:
  //   there must be a whole science to wiring i'm unaware of
endmodule
