// Logisim project lib_LevelToFanspeed.circ as structural Verilog: 2 circuits, main circuit levelToFanspeed
module levelToFanspeed (
  input  X,
  input  Y,
  input  Z,
  input  CLK,
  output A_bar,
  output B_bar,
  output C_bar,
  output A,
  output B,
  output C
);

  wire and_1_out, and_2_out, and_3_out, and_4_out, and_5_out, and_6_out, and_7_out, and_8_out, and_9_out,
       and_10_out, and_11_out, and_12_out, and_13_out, and_14_out, and_15_out, and_16_out, and_17_out,
       and_18_out, not_1_out, not_2_out, not_3_out, or_1_out, or_2_out, or_3_out, or_4_out, or_5_out;

  not not_1 (not_1_out, X);
  not not_2 (not_2_out, Y);
  not not_3 (not_3_out, Z);
  and and_1 (and_1_out, A, X);
  and and_2 (and_2_out, X, Y, Z);
  and and_3 (and_3_out, C, Y, X);
  and and_4 (and_4_out, B, Z, X);
  and and_5 (and_5_out, B, X, Y);
  and and_6 (and_6_out, B, C, X);
  and and_7 (and_7_out, A, Y, not_1_out);
  and and_8 (and_8_out, X, B_bar, not_2_out, C);
  and and_9 (and_9_out, not_2_out, X, Z, A_bar, B_bar);
  and and_10 (and_10_out, A, not_1_out, Z);
  and and_11 (and_11_out, A_bar, B_bar, C_bar, X, Y, not_3_out);
  and and_12 (and_12_out, A_bar, B_bar, C_bar, X, not_3_out);
  and and_13 (and_13_out, B_bar, C, X, not_2_out, Z);
  and and_14 (and_14_out, B, C_bar, not_1_out, Y, Z);
  and and_15 (and_15_out, B, C, not_1_out, Y, not_3_out);
  or or_1 (or_1_out, and_1_out, and_2_out, and_3_out);
  or or_2 (or_2_out, and_4_out, and_5_out, and_6_out);
  and and_16 (and_16_out, B, C_bar, X, not_2_out, not_3_out);
  and and_17 (and_17_out, A_bar, C_bar, X, not_3_out, not_2_out);
  and and_18 (and_18_out, B, C, not_1_out, Y, Z);
  or or_3 (or_3_out, or_1_out, or_2_out);
  or or_4 (or_4_out, and_7_out, and_8_out, and_9_out, and_11_out, and_16_out, and_18_out);
  or or_5 (or_5_out, and_12_out, and_13_out, and_14_out, and_10_out, and_15_out, and_17_out);
  D_Flip_Flop d_ff_1 (.D(or_3_out), .clk(CLK), .Q(A), .Qn(A_bar));  // open: preset, reset
  D_Flip_Flop d_ff_2 (.D(or_4_out), .clk(CLK), .Q(B), .Qn(B_bar));  // open: preset, reset
  D_Flip_Flop d_ff_3 (.D(or_5_out), .clk(CLK), .Q(C), .Qn(C_bar));  // open: preset, reset
endmodule

module testSandbox (
);

  wire clock_1_out;
  wire [2:0] leveltofanspeed_1_c, slider_1_out;

  Slider #(.value('h3), .width(3)) slider_1 (.out(slider_1_out));
  Clock clock_1 (.out(clock_1_out));
  levelToFanspeed leveltofanspeed_1 (
    .X(slider_1_out[2]), .Y(slider_1_out[1]), .Z(slider_1_out[0]), .CLK(clock_1_out),
    .A(leveltofanspeed_1_c[2]), .B(leveltofanspeed_1_c[1]), .C(leveltofanspeed_1_c[0]));  // open: A_bar, B_bar, C_bar
  // Probe on leveltofanspeed_1_c
endmodule
